# Fritzing sketch Esquema (saved by Fritzing 1.0.2b)
breadboards: 2

parts:
  U1 = ESP32-38PinWide [part_number=ESP32-38PinWide]
  VCC1 = Battery block 9V
  HC-SR04_Sensor_1 = HC-SR04 Ultrasonic Distance Sensor
  LED1 = smd LED [color="Red (633nm)" package="1206 [SMD]"]
  LED2 = smd LED [color="Green (555nm)" package="1206 [SMD]"]
  R1 = Resistor [tolerance=±5% resistance=1k package="0402 [SMD]"]
  Q1 = Basic FET N-Channel [package="TO220 [THT]"]
  R2 = Resistor [tolerance=±5% resistance=1k package="0402 [SMD]"]
  Q2 = Basic FET P-Channel [package="TO220 [THT]"]

nets:
  N1: U1.3.3, HC-SR04_Sensor_1.VCC
  GND: U1.GND, VCC1.-, HC-SR04_Sensor_1.GND, Q1.source, Q2.source
  N2: U1.GPIO19, R2.Pin_0
  N3: U1.GPIO21, R1.Pin_0
  N4: U1.GPIO22, HC-SR04_Sensor_1.ECHO
  N5: U1.GPIO23, HC-SR04_Sensor_1.TRIG
  N6: VCC1.+, LED1.anode, LED2.anode
  N7: LED1.cathode, Q1.drain
  N8: LED2.cathode, Q2.drain
  N9: R1.Pin_1, Q1.gate
  N10: R2.Pin_1, Q2.gate

custom parts:
  ESP32-38PinWide: Generic 38-Pin ESP32 with wide format (only access to one side of pins on a breadboard) based on Stephen Lilley's HiLetgo ESP-WROOM-32 ESP32 ESP-32S Development Board.
